# Fritzing sketch dogscale strip board (saved by Fritzing 1.0.1rc)
stripboards: 2

parts:
  S1 = Load Sensor - 50kg [part_number=SEN-10245]
  S2 = Load Sensor - 50kg [part_number=SEN-10245]
  S3 = Load Sensor - 50kg [part_number=SEN-10245]
  S4 = Load Sensor - 50kg [part_number=SEN-10245]
  Bauteil2 = HX711 Weighing Sensor Module MR  # not connected
  A1 = SparkFun RJ45 Breakout v11  # not connected
  LCD2 = 2.8" SPI TFT Module [part_number=MSP2807]
  Mod3 = Amica NodeMCU DEVKIT 1.0
  A3 = SparkFun RJ45 Breakout v11

nets:
  N1: S1.B, S2.B
  N2: S1.W, S4.W
  N3: S2.W, S3.W
  N4: S3.B, S4.B
  N5: LCD2.pin1, LCD2.pin8, Mod3.pin1, Mod3.pin_10, Mod3.pin_26, A3.Pin_6
  N6: LCD2.pin2, Mod3.pin2, Mod3.pin_9, Mod3.pin_25, Mod3.pin_29, A3.Pin_3
  N7: LCD2.pin3, Mod3.pin5
  N8: LCD2.pin4, Mod3.pin_11
  N9: LCD2.pin5, Mod3.pin_12
  N10: LCD2.pin6, LCD2.pin12, Mod3.pin6
  N11: LCD2.pin7, LCD2.pin10, Mod3.pin8
  N12: LCD2.pin9, LCD2.pin13, Mod3.pin7
  N13: LCD2.pin11, Mod3.pin_15
  N14: Mod3.pin_13, A3.Pin_4
  N15: Mod3.pin_14, A3.Pin_5

notes:
  1
  2
  3
  4

custom parts:
  Load Sensor - 50kg: Half-wheatstone bridge Load Cell modified from the Fritzing Repo This load sensor, sometimes called a strain gauge, is the same one found in digital bathroom scales (you know, the ones you use in January for your New Year's resolutions, and then forget about a month later). This sensor can measure up to about 110 pounds.
  HX711 Weighing Sensor Module MR: HX711 is a precision 24-bit analog-to-digital converter (ADC) designed for weigh scales and industrial control applications to interface directly with a bridge sensor.
  SparkFun RJ45 Breakout v11: SparkFun RJ45 Breakout v11 breakout board.
  2.8" SPI TFT Module: A generic 2.8 inch LCD TFT 320x240 display with touchscreen and SD card slot. Uses the ILI9341 controller, like the Adafruit displays of this size uses.
